# Fritzing sketch Trafikklys (saved by Fritzing 0.9.3b)
breadboards: 1

parts:
  Part1 = Arduino Uno (Rev3)
  LED2 = LED - 5mm [color="Red (633nm)" package="5 mm [THT]"]
  LED3 = LED - 5mm [color="Yellow (595nm)" package="5 mm [THT]"]
  LED4 = LED - 5mm [color="Green (570nm)" package="5 mm [THT]"]
  LED5 = LED - 5mm [color="Red (633nm)" package="5 mm [THT]"]
  LED6 = LED - 5mm [color="Green (570nm)" package="5 mm [THT]"]  # not connected
  S1 = Pushbutton [package="[SMD]"]
  R1 = Resistor [tolerance=±5% resistance=220 package="0805 [SMD]"]
  R2 = Resistor [tolerance=±5% resistance=220 package="0805 [SMD]"]
  R3 = Resistor [tolerance=±5% resistance=220 package="0805 [SMD]"]
  R4 = Resistor [tolerance=±5% resistance=220 package="0805 [SMD]"]
  R5 = Resistor [tolerance=±5% resistance=220 package="0805 [SMD]"]
  R6 = Resistor [tolerance=±5% resistance=220 package="0805 [SMD]"]
  J1 = Basic Servo

nets:
  N1: Part1.D8, R3.Pin_1
  N2: Part1.D11_PWM/MOSI, R1.Pin_1
  N3: Part1.D2, S1.Pin_3, S1.Pin_4, R6.Pin_1
  N4: Part1.D3_PWM, J1.pulse
  N5: Part1.D6_PWM, R5.Pin_1
  N6: Part1.D7, R4.Pin_1
  N7: Part1.3V3, S1.Pin_1, S1.Pin_2
  5V: Part1.5V, J1.vcc
  GND: Part1.GND, LED2.cathode, LED3.cathode, LED4.cathode, LED5.cathode, R6.Pin_0, J1.gnd
  N8: LED2.anode, R1.Pin_0
  N9: LED3.anode, R2.Pin_0
  N10: LED4.anode, R3.Pin_0
  N11: LED5.anode, R4.Pin_0
