# Fritzing sketch oving_3 (saved by Fritzing 0.9.3b)
breadboards: 1

parts:
  Part1 = Arduino Uno (Rev3)
  J1 = Piezo Speaker
  R1 = Resistor [tolerance=±5% resistance=220 package="2512 [SMD]"]  # not connected
  Part2 = Bluetooth HC-05 Macho

nets:
  N1: Part1.D10_PWM/SS, Part2.RXD
  N2: Part1.D11_PWM/MOSI, Part2.TXD
  5V: Part1.5V, Part2.VCC
  GND: Part1.GND, J1.pin1, Part2.GND
