# Fritzing sketch robot (saved by Fritzing 0.9.3b)
breadboards: 1

parts:
  Part1 = Arduino Uno (Rev3) - ICSP
  Part2 = Bluetooth HC-05 Macho
  hc-sr1 = hc-sr04

nets:
  N1: Part1.D1/TX, Part2.TXD
  N2: Part1.D2, hc-sr1.Trig
  N3: Part1.D3_PWM, hc-sr1.Echo
  N4: Part1.D6_PWM, Part2.RXD
  VCC: Part1.5V, Part2.VCC, hc-sr1.VCC
  GND: Part1.GND, Part2.GND, hc-sr1.GND
